# Fritzing sketch watz (saved by Fritzing 0.9.1b)
breadboards: 1

parts:
  Part1 = Spark Core (v1.0)
  Q1 = NPN-Transistor [part_number=TSL251R-LF package="SOT-23 [SMD]"]

nets:
  N1: Part1.GND, Q1.2
  N2: Part1.D0, Q1.1
  N3: Part1.3V3, Q1.0
